# Fritzing sketch circuit_diagram (saved by Fritzing 0.9.5d)
breadboards: 1

parts:
  Raspberry_Pi1 = Raspberry Pi 2
  M1 = DC Motor
  U1 = TA7291P [package=TA7291P]
  U2 = TA7291P [package=TA7291P]
  VCC2 = 4 x AAA Battery Mount
  M3 = DC Motor
  R1 = Resistor [tolerance=±5% resistance=4.7k package="1206 [SMD]"]
  R2 = Resistor [tolerance=±5% resistance=4.7k package="1206 [SMD]"]

nets:
  3V3: Raspberry_Pi1.3v3, Raspberry_Pi1.3V3, U1.Vcc, U2.Vcc
  N1: Raspberry_Pi1.GPIO17, U1.IN1
  N2: Raspberry_Pi1.GPIO27, U2.IN1
  N3: Raspberry_Pi1.GPIO24, U2.IN2
  N4: Raspberry_Pi1.GPIO18, U1.IN2
  GND: Raspberry_Pi1.GND, U1.GND, U2.GND, VCC2.-
  N5: M1.pin_1, U1.OUT2
  N6: M1.pin_2, U1.OUT1
  N7: U1.Vref, R1.Pin_0
  N8: U1.Vs, U2.Vs, VCC2.+, R1.Pin_1, R2.Pin_1
  N9: U2.OUT1, M3.pin_2
  N10: U2.Vref, R2.Pin_0
  N11: U2.OUT2, M3.pin_1

custom parts:
  TA7291P: The IC are Full-Bridge Driver. 4 modes available (CW / CCW / STOP / BRAKE) and PWM control. Output current:1.0 A (AVE.) 2.0 A (PEAK)

// code stored in the sketch: color-fader.ino
/*
  _____       .__  __         .__                
_/ ____\______|__|/  |________|__| ____    ____  
\   __\\_  __ \  \   __\___   /  |/    \  / ___\ 
 |  |   |  | \/  ||  |  /    /|  |   |  \/ /_/  >
 |__|   |__|  |__||__| /_____ \__|___|  /\___  / 
                             \/       \//_____/  
          __                 __                  __   .__  __   
  _______/  |______ ________/  |_  ___________  |  | _|__|/  |_ 
 /  ___/\   __\__  \\_  __ \   __\/ __ \_  __ \ |  |/ /  \   __\
 \___ \  |  |  / __ \|  | \/|  | \  ___/|  | \/ |    <|  ||  |  
/____  > |__| (____  /__|   |__|  \___  >__|    |__|_ \__||__|  
     \/            \/                 \/             \/         

Example      RGB LED Fader
Autor        Stefan Hermann
Date         16.06.2011

Description  This example lets you fade through the colors of a RGB LED.

NOTE         This example expects an RGB LED of the type "common anode".
             If your type is "common cathode", the brightness will be reversed.

*/

int LEDGreen=9;
int LEDBlue=10;
int LEDRed=11;


int sensorPin=0;
int val;

void setup(){
  Serial.begin(9600);
  pinMode(LEDRed,OUTPUT);
  pinMode(LEDGreen,OUTPUT);
  pinMode(LEDBlue,OUTPUT);  
}

void loop(){
  
  val=map(analogRead(sensorPin),0,1024,0,900);
  Serial.println(val);
  if (val<150) {
    analogWrite(LEDRed,0);
    analogWrite(LEDBlue,255); 
    analogWrite(LEDGreen,255);    
  } else if (val<300) {
    analogWrite(LEDRed,map(val,150,300,0,255));
    analogWrite(LEDBlue,map(val,150,300,255,0)); 
    analogWrite(LEDGreen,255);
  } else if (val<450) {
    analogWrite(LEDRed,255);
    analogWrite(LEDBlue,0); 
    analogWrite(LEDGreen,255);  
  } else if (val<600) {
    analogWrite(LEDRed,255);
    analogWrite(LEDBlue,map(val,450,600,0,255)); 
    analogWrite(LEDGreen,map(val,450,600,255,0));
  } else if (val<750) {
    analogWrite(LEDRed,255);
    analogWrite(LEDBlue,255); 
    analogWrite(LEDGreen,0);  
  } else if (val<900) {
    analogWrite(LEDRed,map(val,750,900,255,0));
    analogWrite(LEDBlue,255); 
    analogWrite(LEDGreen,map(val,750,900,0,255));
  }
  delay(10);
}
